// Logisim project elevator_0.1.circ as structural Verilog: 4 circuits, main circuit main
module main (
  input  [7:0] in_1,
  output out_2,
  output [2:0] out_3,
  output out_4,
  output [7:0] D0,
  output [7:0] out_6,
  output [7:0] out_7,
  output [7:0] D2
);

  wire button_2_out, clock_1_out, comparator_1_out_5, INIT, or_1_out, or_2_out, or_3_out, or_4_out,
       priority_encoder_1_gs;
  wire [1:0] priority_encoder_1_out;
  wire [7:0] _1_2_out, _1_3_out, _1_out, multiplexer_1_out;

  Button button_1 (.out(INIT));
  Button _1 (.out(_1_out[0]));
  Button _2 (.out(_1_out[1]));
  Button _3 (.out(_1_out[2]));
  Button _4 (.out(_1_out[3]));
  Button _5 (.out(_1_out[4]));
  Button _6 (.out(_1_out[5]));
  Button _7 (.out(_1_out[6]));
  Button _8 (.out(_1_out[7]));
  Button _1_2 (.out(_1_2_out[0]));
  Button _2_2 (.out(_1_2_out[1]));
  Button _3_2 (.out(_1_2_out[2]));
  Button _4_2 (.out(_1_2_out[3]));
  Button _5_2 (.out(_1_2_out[4]));
  Button _6_2 (.out(_1_2_out[5]));
  Button _7_2 (.out(_1_2_out[6]));
  Button _8_2 (.out(_1_2_out[7]));
  Button _1_3 (.out(_1_3_out[0]));
  Button _2_3 (.out(_1_3_out[1]));
  Button _3_3 (.out(_1_3_out[2]));
  Button _4_3 (.out(_1_3_out[3]));
  Button _5_3 (.out(_1_3_out[4]));
  Button _6_3 (.out(_1_3_out[5]));
  Button _7_3 (.out(_1_3_out[6]));
  Button _8_3 (.out(_1_3_out[7]));
  _8bit_JK_FF u_8bit_jk_ff_1 (.J(_1_out), .K(out_7), .Q(D0));
  _8bit_JK_FF u_8bit_jk_ff_2 (.J(_1_2_out), .K(out_7), .Q(out_6));
  _8bit_JK_FF u_8bit_jk_ff_3 (.J(_1_3_out), .K(out_7), .Q(D2));
  or or_1 (or_1_out, D0[7], D0[6], D0[5], D0[4], D0[3], D0[2], D0[1], D0[0]);
  or or_2 (or_2_out, out_6[7], out_6[6], out_6[5], out_6[4], out_6[3], out_6[2], out_6[1], out_6[0]);
  or or_3 (or_3_out, D2[7], D2[6], D2[5], D2[4], D2[3], D2[2], D2[1], D2[0]);
  Priority_Encoder #(.select(2)) priority_encoder_1 (
    .in0(or_3_out), .in1(or_2_out), .in2(or_1_out), .out(priority_encoder_1_out), .gs(priority_encoder_1_gs));  // open: in3, en_out, en_in
  Comparator comparator_1 (
    .in_1(multiplexer_1_out), .in_2(out_7), .out_5(comparator_1_out_5));  // open: out_3, out_4, out_6
  Multiplexer #(.select(2), .width(8)) multiplexer_1 (
    .in0(D2), .in1(out_6), .in2(D0), .out(multiplexer_1_out), .sel(priority_encoder_1_out),
    .en(priority_encoder_1_gs));  // open: in3
  Clock clock_1 (.out(clock_1_out));
  or or_4 (or_4_out, button_2_out, INIT);
  Button button_2 (.out(button_2_out));
  Elevator elevator_1 (
    .INC_DEC_prime(comparator_1_out_5), .Q0(out_7[0]), .Q1(out_7[1]), .Q2(out_7[2]), .Q3(out_7[3]),
    .Q4(out_7[4]), .Q5(out_7[5]), .Q6(out_7[6]), .Q7(out_7[7]), .INIT(or_4_out), .CLK(clock_1_out),
    .EN(priority_encoder_1_gs));
  LED _8_4 (.in(out_7[7]));
  LED _7_4 (.in(out_7[6]));
  LED _6_4 (.in(out_7[5]));
  LED _5_4 (.in(out_7[4]));
  LED _4_4 (.in(out_7[3]));
  LED _3_4 (.in(out_7[2]));
  LED _2_4 (.in(out_7[1]));
  LED _1_4 (.in(out_7[0]));
  Priority_Encoder priority_encoder_2 (
    .in0(in_1[0]), .in1(in_1[1]), .in2(in_1[2]), .in3(in_1[3]), .in4(in_1[4]), .in5(in_1[5]), .in6(in_1[6]),
    .in7(in_1[7]), .out(out_3), .gs(out_4), .en_out(out_2));  // open: en_in

  // Notes on the sheet:
  //   Init Elevator
  //   Elevator  Buttons
  //   Up  Buttons
  //   Down  Buttons
  //   D1
  //   D0 > 0?
  //   D1 > 0?
  //   D2 > 0?
  //   FSM
  //   D>Q?
  //   Elevator
  //   Q
  //   INIT ELEVATOR
  //   Floor
endmodule

module Elevator (
  input  INC_DEC_prime,
  input  CLK,
  input  EN,
  input  INIT,
  output Q0,
  output Q1,
  output Q2,
  output Q3,
  output Q4,
  output Q5,
  output Q6,
  output Q7
);

  wire and_1_out, and_2_out, and_3_out, and_4_out, and_5_out, and_6_out, and_7_out, and_8_out, and_9_out,
       and_10_out, and_11_out, and_12_out, and_13_out, and_14_out, and_15_out, and_16_out, not_1_out,
       or_1_out, or_2_out, or_3_out, or_4_out, or_5_out, or_6_out, or_7_out, or_8_out;

  not not_1 (not_1_out, INC_DEC_prime);
  or or_1 (or_1_out, Q0, and_1_out);
  and and_1 (and_1_out, not_1_out, Q1);
  and and_2 (and_2_out, Q0, INC_DEC_prime);
  and and_3 (and_3_out, not_1_out, Q2);
  and and_4 (and_4_out, Q1, INC_DEC_prime);
  and and_5 (and_5_out, not_1_out, Q3);
  and and_6 (and_6_out, Q2, INC_DEC_prime);
  and and_7 (and_7_out, not_1_out, Q4);
  and and_8 (and_8_out, Q3, INC_DEC_prime);
  and and_9 (and_9_out, not_1_out, Q5);
  and and_10 (and_10_out, Q4, INC_DEC_prime);
  and and_11 (and_11_out, not_1_out, Q6);
  and and_12 (and_12_out, Q5, INC_DEC_prime);
  and and_13 (and_13_out, not_1_out, Q7);
  and and_14 (and_14_out, Q6, INC_DEC_prime);
  or or_2 (or_2_out, and_14_out, Q7);
  and and_15 (and_15_out, not_1_out, or_1_out);
  or or_3 (or_3_out, and_2_out, and_3_out);
  or or_4 (or_4_out, and_4_out, and_5_out);
  or or_5 (or_5_out, and_6_out, and_7_out);
  or or_6 (or_6_out, and_8_out, and_9_out);
  or or_7 (or_7_out, and_10_out, and_11_out);
  or or_8 (or_8_out, and_12_out, and_13_out);
  and and_16 (and_16_out, or_2_out, INC_DEC_prime);
  D_Flip_Flop d_ff_1 (.clk(CLK), .D(and_15_out), .Q(Q0), .preset(INIT), .en(EN));  // open: Qn, reset
  D_Flip_Flop d_ff_2 (.clk(CLK), .D(or_3_out), .Q(Q1), .en(EN), .reset(INIT));  // open: Qn, preset
  D_Flip_Flop d_ff_3 (.clk(CLK), .D(or_4_out), .Q(Q2), .en(EN), .reset(INIT));  // open: Qn, preset
  D_Flip_Flop d_ff_4 (.clk(CLK), .D(or_5_out), .Q(Q3), .en(EN), .reset(INIT));  // open: Qn, preset
  D_Flip_Flop d_ff_5 (.clk(CLK), .D(or_6_out), .Q(Q4), .en(EN), .reset(INIT));  // open: Qn, preset
  D_Flip_Flop d_ff_6 (.clk(CLK), .D(or_7_out), .Q(Q5), .en(EN), .reset(INIT));  // open: Qn, preset
  D_Flip_Flop d_ff_7 (.clk(CLK), .D(or_8_out), .Q(Q6), .en(EN), .reset(INIT));  // open: Qn, preset
  D_Flip_Flop d_ff_8 (.clk(CLK), .D(and_16_out), .Q(Q7), .en(EN), .reset(INIT));  // open: Qn, preset
endmodule

module _8bit_JK_FF (
  input  [7:0] J,
  input  [7:0] K,
  output [7:0] Q
);

  wire or_1_out, or_2_out, or_3_out, or_4_out, or_5_out, or_6_out, or_7_out, or_8_out;

  or or_1 (or_1_out, J[0], K[0]);
  or or_2 (or_2_out, J[1], K[1]);
  or or_3 (or_3_out, J[2], K[2]);
  or or_4 (or_4_out, J[3], K[3]);
  or or_5 (or_5_out, J[4], K[4]);
  or or_6 (or_6_out, J[5], K[5]);
  or or_7 (or_7_out, J[6], K[6]);
  or or_8 (or_8_out, J[7], K[7]);
  J_K_Flip_Flop j_k_ff_1 (.J(J[0]), .clk(or_1_out), .K(K[0]), .Q(Q[0]), .en(or_1_out));  // open: Qn, preset, reset
  J_K_Flip_Flop j_k_ff_2 (.J(J[1]), .clk(or_2_out), .K(K[1]), .Q(Q[1]), .en(or_2_out));  // open: Qn, preset, reset
  J_K_Flip_Flop j_k_ff_3 (.J(J[2]), .clk(or_3_out), .K(K[2]), .Q(Q[2]), .en(or_3_out));  // open: Qn, preset, reset
  J_K_Flip_Flop j_k_ff_4 (.J(J[3]), .clk(or_4_out), .K(K[3]), .Q(Q[3]), .en(or_4_out));  // open: Qn, preset, reset
  J_K_Flip_Flop j_k_ff_5 (.J(J[4]), .clk(or_5_out), .K(K[4]), .Q(Q[4]), .en(or_5_out));  // open: Qn, preset, reset
  J_K_Flip_Flop j_k_ff_6 (.J(J[5]), .clk(or_6_out), .K(K[5]), .Q(Q[5]), .en(or_6_out));  // open: Qn, preset, reset
  J_K_Flip_Flop j_k_ff_7 (.J(J[6]), .clk(or_7_out), .K(K[6]), .Q(Q[6]), .en(or_7_out));  // open: Qn, preset, reset
  J_K_Flip_Flop j_k_ff_8 (.J(J[7]), .clk(or_8_out), .K(K[7]), .Q(Q[7]), .en(or_8_out));  // open: Qn, preset, reset
endmodule

module Comparator (
  input  [7:0] in_1,
  input  [7:0] in_2,
  output [2:0] out_3,
  output out_4,
  output out_5,
  output out_6
);

  wire bitselector_1_out, bitselector_2_out, priority_encoder_1_gs;
  wire [7:0] xor_1_out;

  assign xor_1_out = in_1 ^ in_2;  // XOR_Gate xor_1, 8 bits wide
  BitSelector bitselector_1 (.in(in_1), .out(bitselector_1_out), .sel(out_3));
  BitSelector bitselector_2 (.in(in_2), .out(bitselector_2_out), .sel(out_3));
  Priority_Encoder priority_encoder_1 (
    .in0(xor_1_out[0]), .in1(xor_1_out[1]), .in2(xor_1_out[2]), .in3(xor_1_out[3]), .in4(xor_1_out[4]),
    .in5(xor_1_out[5]), .in6(xor_1_out[6]), .in7(xor_1_out[7]), .out(out_3), .en_in(1'b1),
    .gs(priority_encoder_1_gs));  // open: en_out
  not not_1 (out_4, priority_encoder_1_gs);
  and and_1 (out_5, bitselector_1_out, priority_encoder_1_gs);
  and and_2 (out_6, bitselector_2_out, priority_encoder_1_gs);
endmodule
